# Fritzing sketch yedek (saved by Fritzing 0.9.3b)
breadboards: 1

parts:
  Parça2 = Arduino Uno (Rev3)
  IC2 = DIP - 10 pins [chip_label=TEA5767 package="DIP (Dual Inline) [THT]"]
  SPKR2 = Loudspeaker  # not connected
  LCD2 = LCD screen
  R1_(Ekran)1 = Rotary Potentiometer (Small) [maximum_resistance=100kΩ package=THT]
  R2_(Kanal_switch)1 = Rotary Potentiometer (Small) [maximum_resistance=100kΩ package=THT]

nets:
  N1: Parça2.A0, R2_(Kanal_switch)1.wiper
  N2: Parça2.A4/SDA, IC2.DATA
  N3: Parça2.A5/SCL, IC2.SCLK
  N4: Parça2.D11_PWM/MOSI, LCD2.E
  N5: Parça2.D12/MISO, LCD2.RS
  GND: Parça2.GND, IC2.GND, LCD2.VSS, LCD2.R/W, LCD2.LED-, R1_(Ekran)1.leg2, R2_(Kanal_switch)1.leg2
  N6: Parça2.D2, LCD2.DB7
  N7: Parça2.D3_PWM, LCD2.DB6
  N8: Parça2.D4, LCD2.DB5
  N9: Parça2.D5_PWM, LCD2.DB4
  5V: Parça2.5V, IC2.VCC, LCD2.VDD, LCD2.LED+, R1_(Ekran)1.leg1, R2_(Kanal_switch)1.leg1
  N10: LCD2.V0, R1_(Ekran)1.wiper

custom parts:
  DIP - 10 pins: A DIP stand-in part for whatever IC you want. With 10 pins on a 300mil dual inline package (DIP) footprint.
